// Logisim project BinaerZuSiebenSegmentWandler.circ as structural Verilog: 2 circuits, main circuit BinaerZu7SegmentWandler
module BinaerZu7SegmentWandler (
  input  A,
  input  B,
  input  C,
  input  D
);

  wire and_1_out, and_2_out, and_3_out, and_4_out, and_5_out, and_6_out, and_7_out, and_8_out, and_9_out,
       and_10_out, and_11_out, and_12_out, and_13_out, and_14_out, and_15_out, and_16_out, and_17_out,
       not_1_out, not_2_out, not_3_out, or_1_out, or_2_out, or_3_out, or_4_out, or_5_out, or_6_out, or_7_out,
       or_8_out, or_9_out, or_10_out, or_11_out, or_12_out, or_13_out, or_14_out, or_15_out, or_16_out,
       or_17_out;

  not not_1 (not_1_out, B);
  not not_2 (not_2_out, C);
  not not_3 (not_3_out, D);
  and and_1 (and_1_out, B, D);
  and and_2 (and_2_out, not_1_out, D);
  and and_3 (and_3_out, not_1_out, C);
  and and_4 (and_4_out, B, not_2_out);
  or or_1 (or_1_out, D, B);
  and and_5 (and_5_out, B, not_2_out);
  and and_6 (and_6_out, C, not_3_out);
  and and_7 (and_7_out, A, not_3_out);
  and and_8 (and_8_out, B, not_2_out);
  and and_9 (and_9_out, B, not_3_out);
  and and_10 (and_10_out, not_1_out, C);
  and and_11 (and_11_out, B, not_2_out);
  and and_12 (and_12_out, C, not_3_out);
  or or_2 (or_2_out, C, and_1_out);
  or or_3 (or_3_out, and_2_out, and_3_out);
  and and_13 (and_13_out, and_4_out, not_3_out);
  and and_14 (and_14_out, C, D);
  or or_4 (or_4_out, or_1_out, A);
  and and_15 (and_15_out, not_1_out, C);
  and and_16 (and_16_out, and_5_out, D);
  and and_17 (and_17_out, C, not_3_out);
  or or_5 (or_5_out, and_6_out, and_7_out);
  or or_6 (or_6_out, and_8_out, and_9_out);
  or or_7 (or_7_out, and_10_out, and_11_out);
  or or_8 (or_8_out, A, and_12_out);
  or or_9 (or_9_out, or_2_out, A);
  or or_10 (or_10_out, or_3_out, and_13_out);
  or or_11 (or_11_out, or_10_out, or_12_out);
  or or_12 (or_12_out, and_14_out, A);
  or or_13 (or_13_out, and_15_out, and_16_out);
  or or_14 (or_14_out, or_13_out, or_15_out);
  or or_15 (or_15_out, and_17_out, A);
  or or_16 (or_16_out, or_6_out, A);
  or or_17 (or_17_out, or_7_out, or_8_out);
  _7_Segment_Display u_7_segment_display_1 (
    .g(or_17_out), .f(or_16_out), .a(or_9_out), .b(or_11_out), .e(or_5_out), .d(or_14_out), .c(or_4_out));  // open: dp
endmodule

module Schaltplan (
  input  A,
  input  B,
  input  C,
  input  D
);

  wire n7404_1_pin2, n7404_1_pin10, n7404_1_pin12, n7408_1_pin3, n7408_1_pin6, n7408_1_pin8, n7408_1_pin11,
       n7408_2_pin3, n7408_2_pin6, n7408_2_pin8, n7408_2_pin10, n7408_2_pin11, n7408_3_pin6, n7408_3_pin8,
       n7408_3_pin11, n7408_4_pin3, n7408_4_pin6, n7408_4_pin8, n7408_4_pin11, n7408_5_p4, n7432_1_pin8,
       n7432_1_pin11, n7432_2_pin3, n7432_2_pin6, n7432_2_pin11, n7432_3_pin3, n7432_3_pin6, n7432_3_pin11,
       n7432_4_pin1, n7432_4_pin2, n7432_4_pin3, n7432_5_pin1, n7432_5_pin2, n7432_5_pin3, n7432_5_pin4,
       n7432_5_pin6, n7432_5_pin8;

  _7404 u_7404_1 (
    .pin1(D), .pin2(n7404_1_pin2), .pin13(B), .pin12(n7404_1_pin12), .pin11(C), .pin10(n7404_1_pin10));  // open: pin3, pin4, pin5, pin6, pin9, pin8
  _7408 u_7408_1 (
    .pin1(n7404_1_pin12), .pin2(C), .pin3(n7408_1_pin3), .pin4(B), .pin5(n7404_1_pin10), .pin6(n7408_1_pin6),
    .pin13(B), .pin12(D), .pin11(n7408_1_pin11), .pin10(n7404_1_pin12), .pin9(D), .pin8(n7408_1_pin8));
  _7432 u_7432_1 (
    .pin13(n7408_1_pin8), .pin12(n7408_1_pin3), .pin11(n7432_1_pin11), .pin10(n7408_1_pin11), .pin9(C),
    .pin8(n7432_1_pin8));  // open: pin1, pin2, pin3, pin4, pin5, pin6
  _7408 u_7408_2 (
    .pin1(C), .pin2(D), .pin3(n7408_2_pin3), .pin4(n7404_1_pin12), .pin5(C), .pin6(n7408_2_pin6),
    .pin13(n7408_1_pin6), .pin12(n7404_1_pin2), .pin11(n7408_2_pin11), .pin10(n7408_2_pin10), .pin9(D),
    .pin8(n7408_2_pin8));
  _7432 u_7432_2 (
    .pin1(n7432_1_pin11), .pin2(n7408_2_pin11), .pin3(n7432_2_pin3), .pin4(n7408_2_pin3), .pin5(A),
    .pin6(n7432_2_pin6), .pin13(n7432_1_pin8), .pin12(A), .pin11(n7432_2_pin11));  // open: pin10, pin9, pin8
  _7408 u_7408_3 (
    .pin1(B), .pin2(n7404_1_pin10), .pin3(n7408_2_pin10), .pin4(A), .pin5(n7404_1_pin2), .pin6(n7408_3_pin6),
    .pin13(C), .pin12(n7404_1_pin2), .pin11(n7408_3_pin11), .pin10(C), .pin9(n7404_1_pin2),
    .pin8(n7408_3_pin8));
  _7408 u_7408_4 (
    .pin1(n7404_1_pin12), .pin2(C), .pin3(n7408_4_pin3), .pin4(B), .pin5(n7404_1_pin10), .pin6(n7408_4_pin6),
    .pin13(n7404_1_pin2), .pin12(B), .pin11(n7408_4_pin11), .pin10(n7404_1_pin10), .pin9(B),
    .pin8(n7408_4_pin8));
  // _7408 7408_5: pin names not known; wires that end beside it: 1'b1, n7404_1_pin2, C, n7408_5_p4, 1'b0
  _7432 u_7432_3 (
    .pin1(D), .pin2(B), .pin3(n7432_3_pin3), .pin4(n7432_3_pin3), .pin5(A), .pin6(n7432_3_pin6),
    .pin13(n7432_2_pin3), .pin12(n7432_2_pin6), .pin11(n7432_3_pin11));  // open: pin10, pin9, pin8
  _7432 u_7432_4 (
    .pin1(n7432_4_pin1), .pin2(n7432_4_pin2), .pin3(n7432_4_pin3), .pin4(n7408_3_pin11), .pin5(A),
    .pin6(n7432_4_pin2), .pin13(n7408_2_pin8), .pin12(n7408_2_pin6), .pin11(n7432_4_pin1));  // open: pin10, pin9, pin8
  _7432 u_7432_5 (
    .pin1(n7432_5_pin1), .pin2(n7432_5_pin2), .pin3(n7432_5_pin3), .pin4(n7432_5_pin4), .pin5(A),
    .pin6(n7432_5_pin6), .pin13(n7408_4_pin8), .pin12(n7408_4_pin11), .pin11(n7432_5_pin4),
    .pin10(n7408_3_pin6), .pin9(n7408_3_pin8), .pin8(n7432_5_pin8));
  _7432 u_7432_6 (
    .pin1(n7408_4_pin6), .pin2(n7408_4_pin3), .pin3(n7432_5_pin1), .pin4(A), .pin5(n7408_5_p4),
    .pin6(n7432_5_pin2));  // open: pin13, pin12, pin11, pin10, pin9, pin8
  _7_Segment_Display u_7_segment_display_1 (
    .g(n7432_5_pin3), .f(n7432_5_pin6), .a(n7432_2_pin11), .b(n7432_3_pin11), .e(n7432_5_pin8),
    .d(n7432_4_pin3), .c(n7432_3_pin6));  // open: dp

  // Notes on the sheet:
  //           7404 / NOT: 1   
  //   7408 / AND: 5
  //           7432 / OR:   6   
endmodule
